# Fritzing sketch ir-to-lwrf-stripboard (saved by Fritzing 0.9.1b)
circuit board: 8.46667cm x 5.64444cm
stripboards: 1

parts:
  C3 = Ceramic Capacitor [capacitance=22pF package="0805 [SMD, multilayer]"]
  C4 = Ceramic Capacitor [capacitance=22pF package="0805 [SMD, multilayer]"]
  XTAL4 = Crystal [frequency="16 Mhz" package=THT]
  RESET = Pushbutton [package="[SMD]"]
  C2 = Electrolytic Capacitor [capacitance=47µF package="100 mil [THT, electrolytic]"]
  C1 = Electrolytic Capacitor [capacitance=0.1µF package="100 mil [THT, electrolytic]"]
  R1 = Resistor [tolerance=±5% resistance=10k package=THT]
  C5 = Ceramic Capacitor [capacitance=100nF package="100 mil [THT, multilayer]"]
  U1 = atmega328 [package=dip]
  C13 = Ceramic Capacitor [capacitance=100nF package="0805 [SMD, multilayer]"]
  LED1 = LED - 5mm [color="Red (633nm)" current=20mA package="5 mm [THT]"]
  J1 = male pin header, 6 pins [form="♂ (male)"]
  ANT = female pin header, 1 pin [form="♀ (female)"]
  J2 = female pin header, 3 pins [form="♀ (female)"]
  D1 = Rectifier Diode [part_number=1N4001 package="300 mil [THT]"]
  CONN1 = USB connector [package=THT]
  R2 = Resistor [tolerance=±5% resistance=150 package=THT]
  U2 = RF-LINK_TX [package=rf-link_tx]
  Part1 = FTDI Basic Programmer

nets:
  GND: C3.0, C4.1, RESET.Pin_1, RESET.Pin_2, C2.-, C1.-, C5.0, U1.GND, LED1.cathode, J1.pin1, J2.pin2, CONN1.GND, CONN1.chassis5, CONN1.chassis6, U2.GND, Part1.GND
  N1: C3.1, XTAL4.pin_0, U1.XLAT1
  N2: C4.0, XTAL4.pin_1, U1.XLAT2
  RESET: RESET.Pin_3, RESET.Pin_4, R1.Pin_1, U1.RESET, C13.1
  5V: C2.+, C1.+, R1.Pin_0, C5.1, U1.VCC, U1.AVCC, U1.AREF, J1.pin3, J2.pin3, D1.cathode, U2.+5V, Part1.POWER
  RX: U1.D0_(RX), J1.pin4, Part1.TXO
  TX: U1.D1_(TX), J1.pin5, Part1.RXI
  N3: U1.D5_(PWM), R2.Pin_1
  N4: U1.D8, J2.pin1
  N5: U1.D9_(PWM), U2.DATA
  N6: C13.0, J1.pin6, Part1.DTR
  N7: LED1.anode, R2.Pin_0
  N8: J1.pin2, Part1.CTS
  N9: ANT.pin1, U2.ANT
  N10: D1.anode, CONN1.5V
