# Fritzing sketch ir_to_lwrf (saved by Fritzing 0.9.1b)
stripboards: 1

parts:
  C3 = Ceramic Capacitor [capacitance=22pF package="0805 [SMD, multilayer]"]
  C4 = Ceramic Capacitor [capacitance=22pF package="0805 [SMD, multilayer]"]
  XTAL4 = Crystal [frequency="16 Mhz" package=THT]
  RESET = Pushbutton [package="[SMD]"]
  C2 = Electrolytic Capacitor [capacitance=47µF package="100 mil [THT, electrolytic]"]
  C1 = Electrolytic Capacitor [capacitance=0.1µF package="100 mil [THT, electrolytic]"]
  R1 = Resistor [tolerance=±5% resistance=10k package=THT]
  C5 = Ceramic Capacitor [capacitance=100nF package="100 mil [THT, multilayer]"]
  U1 = atmega328 [package=dip]
  J1 = male pin header, 6 pins [form="♂ (male)"]
  C13 = Ceramic Capacitor [capacitance=100nF package="0805 [SMD, multilayer]"]
  IR1 = TSOP312.., 314.. [package=THT]
  U2 = RF-LINK_TX [part_number=TWS-BS-3 package=rf-link_tx]
  LED1 = LED - 5mm [color="Red (633nm)" package="5 mm [THT]"]
  R2 = Resistor [tolerance=±5% resistance=220 package=THT]

nets (from the schematic view):
  GND: C3.0, C4.1, RESET.Pin_1, RESET.Pin_2, C2.-, C1.-, C5.1, U1.GND, J1.pin1, J1.pin2, IR1.GND, U2.GND, LED1.cathode
  N1: C3.1, XTAL4.pin_0, U1.XLAT1
  N2: C4.0, XTAL4.pin_1, U1.XLAT2
  RESET: RESET.Pin_3, RESET.Pin_4, R1.Pin_1, U1.RESET, C13.1
  5V: C2.+, C1.+, R1.Pin_0, C5.0, U1.VCC, U1.AVCC, U1.AREF, J1.pin3, IR1.Vs, U2.+5V
  RX: U1.D0_(RX), J1.pin4
  TX: U1.D1_(TX), J1.pin5
  N3: U1.D6_(PWM), R2.Pin_1
  N4: U1.D8, U2.DATA
  N5: U1.D9_(PWM), IR1.Data
  N6: J1.pin6, C13.0
  N7: LED1.anode, R2.Pin_0
